# Fritzing sketch esp8266_curtains (saved by Fritzing 0.9.2b)
breadboards: 1

parts:
  U1 = ESP8266 WiFi Module [part_number=ESP8266]
  IC1 = L293D [package=THT]
  M1 = DC Motor
  R1 = Photocell (LDR) [package=THT]
  R2 = Resistor [tolerance=±5% resistance=7k package=THT]
  R3 = Resistor [tolerance=±5% resistance=120 package=THT]
  R4 = Resistor [tolerance=±5% resistance=270 package=THT]
  S1 = SWITCH-MOMENTARY-2 [package=reed_switch_pth]
  U2 = SWITCH_SPDT [package=kps-1290]

nets:
  N1: U1.IO2, U2.S
  N2: U1.IO4, U2.O
  N3: U1.3.3V, U1.CHIP_EN, IC1.+V, R4.Pin_0
  N4: U1.GND, U1.IO15, IC1.0V, R2.Pin_1, R3.Pin_1, S1.2, U2.P
  N5: U1.IO5, IC1.In_2
  N6: U1.T_OUT, R1.pin_0, R2.Pin_0
  N7: U1.IO14, IC1.In_1
  N8: U1.IO12, IC1.Enable_1
  N9: U1.IO13, S1.1
  N10: IC1.Out_1_(_Controlled_by_Enable_1_), M1.pin_2
  N11: IC1.Out_2_(_Controlled_by_Enable_1_), M1.pin_1
  N12: R1.pin_1, R3.Pin_0, R4.Pin_1

notes:
  +12v
  +3.3v (700mA)
